# Fritzing sketch 7 leds for 7 buttons (saved by Fritzing 0.9.2b)
circuit board: 4.61887cm x 1.21849cm
circuit board: 5.424cm x 1.53109cm
breadboards: 2

parts:
  R1 = Resistor [tolerance=±5% resistance=220 package=THT]
  LED6 = LED - 5mm [color="Red (633nm)" package="5 mm [THT]"]
  LED5 = LED - 5mm [color="Red (633nm)" package="5 mm [THT]"]
  LED4 = LED - 5mm [color="Red (633nm)" package="5 mm [THT]"]
  LED3 = LED - 5mm [color="Red (633nm)" package="5 mm [THT]"]
  LED2 = LED - 5mm [color="Red (633nm)" package="5 mm [THT]"]
  LED1 = LED - 5mm [color="Red (633nm)" package="5 mm [THT]"]
  S6 = Pushbutton [package="[THT]"]
  S5 = Pushbutton [package="[THT]"]
  S4 = Pushbutton [package="[THT]"]
  S1 = Pushbutton [package="[THT]"]
  S2 = Pushbutton [package="[THT]"]
  S3 = Pushbutton [package="[THT]"]
  R6 = Resistor [tolerance=±5% resistance=220 package=THT]
  R5 = Resistor [tolerance=±5% resistance=220 package=THT]
  R4 = Resistor [tolerance=±5% resistance=220 package=THT]
  R3 = Resistor [tolerance=±5% resistance=220 package=THT]
  R2 = Resistor [tolerance=±5% resistance=220 package=THT]
  R1_2 = Resistor [tolerance=±5% resistance=220 package=THT]
  J1 = male pin header, 8 pins [form="♂ (male)"]
  J1_2 = male pin header, 7 pins [form="♂ (male)"]
  Part1 = Arduino Uno (Rev3)

nets:
  N1: R1.Pin_0, S6.Pin_3, S6.Pin_4, S5.Pin_3, S5.Pin_4, S4.Pin_3, S4.Pin_4, S1.Pin_3, S1.Pin_4, S2.Pin_3, S2.Pin_4, S3.Pin_3, S3.Pin_4, J1.pin7, J1_2.pin7, Part1.GND
  N2: R1.Pin_1, LED6.cathode, LED5.cathode, LED4.cathode, LED3.cathode, LED2.cathode, LED1.cathode
  N3: LED6.anode, J1_2.pin6, Part1.D13/SCK
  N4: LED5.anode, J1_2.pin5, Part1.D12/MISO
  N5: LED4.anode, J1_2.pin4, Part1.D11_PWM/MOSI
  N6: LED3.anode, J1_2.pin3, Part1.D10_PWM/SS
  N7: LED2.anode, J1_2.pin2, Part1.D9_PWM
  N8: LED1.anode, J1_2.pin1, Part1.D8
  N9: S6.Pin_1, S6.Pin_2, R6.Pin_0, J1.pin1, Part1.D7
  N10: S5.Pin_1, S5.Pin_2, R5.Pin_0, J1.pin2, Part1.D6_PWM
  N11: S4.Pin_1, S4.Pin_2, R4.Pin_0, J1.pin3, Part1.D5_PWM
  N12: S1.Pin_1, S1.Pin_2, R1_2.Pin_0, J1.pin6, Part1.D2
  N13: S2.Pin_1, S2.Pin_2, R2.Pin_0, J1.pin5, Part1.D3_PWM
  N14: S3.Pin_1, S3.Pin_2, R3.Pin_0, J1.pin4, Part1.D4
  N15: R6.Pin_1, R5.Pin_1, R4.Pin_1, R3.Pin_1, R2.Pin_1, R1_2.Pin_1, J1.pin8, Part1.5V

notes:
  5v
  GND
  1
  2
  4
  3
  5
  6
