# Fritzing sketch receiver (saved by Fritzing 0.9.2b)
circuit board: 9.21843cm x 7.83598cm
breadboards: 1

parts:
  Part2 = Arduino Uno (Rev3)
  R6 = Resistor [tolerance=±5% resistance=10 package=THT]
  NRF24L2 = NRF24L01
  C3 = Ceramic Capacitor [capacitance=0.1µF voltage=6.3V part_number=104 package="100 mil [THT, multilayer]"]
  LED4 = LED - 5mm [color="Green (565nm)" package="5 mm [THT]"]

nets:
  N1: Part2.D9_PWM, NRF24L2.CE
  N2: Part2.D10_PWM/SS, NRF24L2.CSN
  N3: Part2.D11_PWM/MOSI, NRF24L2.MOSI
  N4: Part2.D12/MISO, NRF24L2.MISO
  N5: Part2.D13/SCK, NRF24L2.SCK
  GND: Part2.GND, R6.Pin_1, NRF24L2.GND, C3.0
  N6: Part2.D3_PWM, LED4.anode
  3V3: Part2.3V3, NRF24L2.VCC, C3.1
  N7: R6.Pin_0, LED4.cathode

notes:
  Receiver
  The transmitter will send a signal instructing this device to turn the LED on or off.
  3.3v
  5v

custom parts:
  NRF24L01: NRF24L01 module

// code stored in the sketch: receiver.ino
#include "RF24.h"

#define RADIO_CE_PIN 9
#define RADIO_CS_PIN 10
#define RADIO_RETRY_DELAY 15
#define RADIO_RETRY_COUNT 15
#define LED_PIN 3

int msg[1];
RF24 radio(RADIO_CE_PIN,RADIO_CS_PIN);
const uint64_t pipe = 0x12CB46E68BLL; #MUST MATCH

const int TURN_ON_COMMAND = 0x10042;
const int TURN_OFF_COMMAND = 0x10043;

void setup(void){
  
 pinMode(LED_PIN, OUTPUT);
 
 radio.begin();
 radio.setRetries(RADIO_RETRY_DELAY, RADIO_RETRY_COUNT);
 radio.setDataRate(RF24_250KBPS);
 radio.setPayloadSize(1);
 radio.openReadingPipe(1,pipe);
 radio.startListening();
 pinMode(LED_PIN, OUTPUT);
}

void loop(void){

  bool wasDelayed = false;
  
    while (radio.available()){
      
      radio.read(msg,1);

      int command = msg[0];

      if(command == TURN_ON_COMMAND) {
        digitalWrite(LED_PIN, HIGH);
      } else if(command == TURN_OFF_COMMAND) {
        digitalWrite(LED_PIN, LOW);
      }

      delay(10);
      wasDelayed = true;

    }
    
    if(!wasDelayed) {
     delay(10);
    }
 }

// code stored in the sketch: rf_receiver.ino
#include "RF24.h"

#define RADIO_CE_PIN 9
#define RADIO_CS_PIN 10
#define RADIO_RETRY_DELAY 15
#define RADIO_RETRY_COUNT 15
#define LED_PIN 3

int msg[1];
RF24 radio(RADIO_CE_PIN,RADIO_CS_PIN);
const uint64_t pipe = 0x12CB46E68BLL; #MUST MATCH

const int TURN_ON_COMMAND = 0x10042;
const int TURN_OFF_COMMAND = 0x10043;

void setup(void){
  
 pinMode(LED_PIN, OUTPUT);
 
 radio.begin();
 radio.setRetries(RADIO_RETRY_DELAY, RADIO_RETRY_COUNT);
 radio.setDataRate(RF24_250KBPS);
 radio.setPayloadSize(1);
 radio.openReadingPipe(1,pipe);
 radio.startListening();
 pinMode(LED_PIN, OUTPUT);
}

void loop(void){

  bool wasDelayed = false;
  
    while (radio.available()){
      
      radio.read(msg,1);

      int command = msg[0];

      if(command == TURN_ON_COMMAND) {
        digitalWrite(LED_PIN, HIGH);
      } else if(command == TURN_OFF_COMMAND) {
        digitalWrite(LED_PIN, LOW);
      }

      delay(10);
      wasDelayed = true;

    }
    
    if(!wasDelayed) {
     delay(10);
    }
 }

// code stored in the sketch: rf_sender.ino
#include <RF24.h>

#define RADIO_CE_PIN 9
#define RADIO_CS_PIN 10
#define RADIO_RETRY_DELAY 15
#define RADIO_RETRY_COUNT 15
#define SWITCH_PIN 2
#define LED_PIN 3

int msg[1];
int switchState = -999;

RF24 radio(RADIO_CE_PIN,RADIO_CS_PIN);

const uint64_t pipe = 0x12CB46E68BLL; # MUST MATCH

const int TURN_ON_COMMAND = 0x10042;
const int TURN_OFF_COMMAND = 0x10043;
                
void setup(void){
  
 radio.begin();
 radio.setRetries(RADIO_RETRY_DELAY, RADIO_RETRY_COUNT);
 radio.setDataRate(RF24_250KBPS);
 radio.setPayloadSize(1);
 radio.openWritingPipe(pipe);

 pinMode(SWITCH_PIN, INPUT);
 pinMode(LED_PIN, OUTPUT);
}

void loop(void){

  int state = digitalRead(SWITCH_PIN);
  
  if(switchState != state) {
    
    switchState = state;
    int command = TURN_OFF_COMMAND;

    if(state == HIGH) {
      command = TURN_ON_COMMAND;
    }
    
    digitalWrite(LED_PIN, state);
    
    msg[0] = command;
    radio.write(msg, 1);
    
  }

  delay(10);
}

// code stored in the sketch: sender.ino
#include <RF24.h>

#define RADIO_CE_PIN 9
#define RADIO_CS_PIN 10
#define RADIO_RETRY_DELAY 15
#define RADIO_RETRY_COUNT 15
#define SWITCH_PIN 2
#define LED_PIN 3

int msg[1];
int switchState = -999;

RF24 radio(RADIO_CE_PIN,RADIO_CS_PIN);

const uint64_t pipe = 0x12CB46E68BLL; # MUST MATCH

const int TURN_ON_COMMAND = 0x10042;
const int TURN_OFF_COMMAND = 0x10043;
                
void setup(void){
  
 radio.begin();
 radio.setRetries(RADIO_RETRY_DELAY, RADIO_RETRY_COUNT);
 radio.setDataRate(RF24_250KBPS);
 radio.setPayloadSize(1);
 radio.openWritingPipe(pipe);

 pinMode(SWITCH_PIN, INPUT);
 pinMode(LED_PIN, OUTPUT);
}

void loop(void){

  int state = digitalRead(SWITCH_PIN);
  
  if(switchState != state) {
    
    switchState = state;
    int command = TURN_OFF_COMMAND;

    if(state == HIGH) {
      command = TURN_ON_COMMAND;
    }
    
    digitalWrite(LED_PIN, state);
    
    msg[0] = command;
    radio.write(msg, 1);
    
  }

  delay(10);
}
