# Fritzing sketch transmitter (saved by Fritzing 0.9.2b)
circuit board: 9.21843cm x 7.83598cm
breadboards: 1

parts:
  Part1 = Arduino Uno (Rev3)
  R2 = Resistor [tolerance=±5% resistance=10 package=THT]
  S1 = Pushbutton [package="[THT]"]
  NRF24L1 = NRF24L01
  C2 = Ceramic Capacitor [capacitance=0.1µF voltage=6.3V part_number=104 package="100 mil [THT, multilayer]"]
  LED3 = LED - 5mm [color="Red (633nm)" package="5 mm [THT]"]
  R4 = Resistor [tolerance=±5% resistance=10 package=THT]

nets (from the breadboard view):
  N1: Part1.D9_PWM, NRF24L1.CE
  N2: Part1.D10_PWM/SS, NRF24L1.CSN
  N3: Part1.D11_PWM/MOSI, NRF24L1.MOSI
  N4: Part1.D12/MISO, NRF24L1.MISO
  N5: Part1.D13/SCK, NRF24L1.SCK
  GND: Part1.GND, Part1.D2, S1.Pin_3, S1.Pin_4, NRF24L1.GND, C2.0, R4.Pin_1
  N6: Part1.D3_PWM, LED3.anode
  3V3: Part1.3V3, NRF24L1.VCC, C2.1
  N7: Part1.5V, R2.Pin_1
  N8: R2.Pin_0, S1.Pin_1, S1.Pin_2
  N9: LED3.cathode, R4.Pin_0

notes:
  Transmitter
  Press a button to toggle the LED on/off. A receiver should mimic the state of the LED with it's own LED.
  3.3v
  5v

custom parts:
  NRF24L01: NRF24L01 module

// code stored in the sketch: receiver.ino
#include "RF24.h"

#define RADIO_CE_PIN 9
#define RADIO_CS_PIN 10
#define RADIO_RETRY_DELAY 15
#define RADIO_RETRY_COUNT 15
#define LED_PIN 3

int msg[1];
RF24 radio(RADIO_CE_PIN,RADIO_CS_PIN);
const uint64_t pipe = 0x12CB46E68BLL; #MUST MATCH

const int TURN_ON_COMMAND = 0x10042;
const int TURN_OFF_COMMAND = 0x10043;

void setup(void){
  
 pinMode(LED_PIN, OUTPUT);
 
 radio.begin();
 radio.setRetries(RADIO_RETRY_DELAY, RADIO_RETRY_COUNT);
 radio.setDataRate(RF24_250KBPS);
 radio.setPayloadSize(1);
 radio.openReadingPipe(1,pipe);
 radio.startListening();
 pinMode(LED_PIN, OUTPUT);
}

void loop(void){

  bool wasDelayed = false;
  
    while (radio.available()){
      
      radio.read(msg,1);

      int command = msg[0];

      if(command == TURN_ON_COMMAND) {
        digitalWrite(LED_PIN, HIGH);
      } else if(command == TURN_OFF_COMMAND) {
        digitalWrite(LED_PIN, LOW);
      }

      delay(10);
      wasDelayed = true;

    }
    
    if(!wasDelayed) {
     delay(10);
    }
 }

// code stored in the sketch: rf_receiver.ino
#include "RF24.h"

#define RADIO_CE_PIN 9
#define RADIO_CS_PIN 10
#define RADIO_RETRY_DELAY 15
#define RADIO_RETRY_COUNT 15
#define LED_PIN 3

int msg[1];
RF24 radio(RADIO_CE_PIN,RADIO_CS_PIN);
const uint64_t pipe = 0x12CB46E68BLL; #MUST MATCH

const int TURN_ON_COMMAND = 0x10042;
const int TURN_OFF_COMMAND = 0x10043;

void setup(void){
  
 pinMode(LED_PIN, OUTPUT);
 
 radio.begin();
 radio.setRetries(RADIO_RETRY_DELAY, RADIO_RETRY_COUNT);
 radio.setDataRate(RF24_250KBPS);
 radio.setPayloadSize(1);
 radio.openReadingPipe(1,pipe);
 radio.startListening();
 pinMode(LED_PIN, OUTPUT);
}

void loop(void){

  bool wasDelayed = false;
  
    while (radio.available()){
      
      radio.read(msg,1);

      int command = msg[0];

      if(command == TURN_ON_COMMAND) {
        digitalWrite(LED_PIN, HIGH);
      } else if(command == TURN_OFF_COMMAND) {
        digitalWrite(LED_PIN, LOW);
      }

      delay(10);
      wasDelayed = true;

    }
    
    if(!wasDelayed) {
     delay(10);
    }
 }

// code stored in the sketch: rf_sender.ino
#include <RF24.h>

#define RADIO_CE_PIN 9
#define RADIO_CS_PIN 10
#define RADIO_RETRY_DELAY 15
#define RADIO_RETRY_COUNT 15
#define SWITCH_PIN 2
#define LED_PIN 3

int msg[1];
int switchState = -999;

RF24 radio(RADIO_CE_PIN,RADIO_CS_PIN);

const uint64_t pipe = 0x12CB46E68BLL; # MUST MATCH

const int TURN_ON_COMMAND = 0x10042;
const int TURN_OFF_COMMAND = 0x10043;
                
void setup(void){
  
 radio.begin();
 radio.setRetries(RADIO_RETRY_DELAY, RADIO_RETRY_COUNT);
 radio.setDataRate(RF24_250KBPS);
 radio.setPayloadSize(1);
 radio.openWritingPipe(pipe);

 pinMode(SWITCH_PIN, INPUT);
 pinMode(LED_PIN, OUTPUT);
}

void loop(void){

  int state = digitalRead(SWITCH_PIN);
  
  if(switchState != state) {
    
    switchState = state;
    int command = TURN_OFF_COMMAND;

    if(state == HIGH) {
      command = TURN_ON_COMMAND;
    }
    
    digitalWrite(LED_PIN, state);
    
    msg[0] = command;
    radio.write(msg, 1);
    
  }

  delay(10);
}

// code stored in the sketch: sender.ino
#include <RF24.h>

#define RADIO_CE_PIN 9
#define RADIO_CS_PIN 10
#define RADIO_RETRY_DELAY 15
#define RADIO_RETRY_COUNT 15
#define SWITCH_PIN 2
#define LED_PIN 3

int msg[1];
int switchState = -999;

RF24 radio(RADIO_CE_PIN,RADIO_CS_PIN);

const uint64_t pipe = 0x12CB46E68BLL; # MUST MATCH

const int TURN_ON_COMMAND = 0x10042;
const int TURN_OFF_COMMAND = 0x10043;
                
void setup(void){
  
 radio.begin();
 radio.setRetries(RADIO_RETRY_DELAY, RADIO_RETRY_COUNT);
 radio.setDataRate(RF24_250KBPS);
 radio.setPayloadSize(1);
 radio.openWritingPipe(pipe);

 pinMode(SWITCH_PIN, INPUT);
 pinMode(LED_PIN, OUTPUT);
}

void loop(void){

  int state = digitalRead(SWITCH_PIN);
  
  if(switchState != state) {
    
    switchState = state;
    int command = TURN_OFF_COMMAND;

    if(state == HIGH) {
      command = TURN_ON_COMMAND;
    }
    
    digitalWrite(LED_PIN, state);
    
    msg[0] = command;
    radio.write(msg, 1);
    
  }

  delay(10);
}

// code stored in the sketch: transmitter.ino
#include <RF24.h>

#define RADIO_CE_PIN 9
#define RADIO_CS_PIN 10
#define RADIO_RETRY_DELAY 15
#define RADIO_RETRY_COUNT 15
#define SWITCH_PIN 2
#define LED_PIN 3

int msg[1];
int switchState = -999;

RF24 radio(RADIO_CE_PIN,RADIO_CS_PIN);

const uint64_t pipe = 0x12CB46E68BLL; # MUST MATCH

const int TURN_ON_COMMAND = 0x10042;
const int TURN_OFF_COMMAND = 0x10043;
                
void setup(void){
  
 radio.begin();
 radio.setRetries(RADIO_RETRY_DELAY, RADIO_RETRY_COUNT);
 radio.setDataRate(RF24_250KBPS);
 radio.setPayloadSize(1);
 radio.openWritingPipe(pipe);

 pinMode(SWITCH_PIN, INPUT);
 pinMode(LED_PIN, OUTPUT);
}

void loop(void){

  int state = digitalRead(SWITCH_PIN);
  
  if(switchState != state) {
    
    switchState = state;
    int command = TURN_OFF_COMMAND;

    if(state == HIGH) {
      command = TURN_ON_COMMAND;
    }
    
    digitalWrite(LED_PIN, state);
    
    msg[0] = command;
    radio.write(msg, 1);
    
  }

  delay(10);
}
